// Logisim project y86_processor.circ as structural Verilog: 13 circuits, main circuit main
module main (
  output [11:0] ValP
);

  wire clock_1_out;
  wire [3:0] fetch_1_icode, fetch_1_ifun, fetch_1_ra, fetch_1_rb;
  wire [11:0] Program_Counter_q;
  wire [63:0] fetch_1_valc;

  Clock clock_1 (.out(clock_1_out));
  Register #(.width(12)) Program_Counter (.D({12{1'b0}}), .clk(clock_1_out), .Q(Program_Counter_q));  // open: en, clr
  fetch fetch_1 (
    .clk(clock_1_out), .PC(Program_Counter_q), .icode(fetch_1_icode), .ifun(fetch_1_ifun), .rA(fetch_1_ra),
    .rB(fetch_1_rb), .valC(fetch_1_valc), .ValP(ValP));
  decode decode_1 ();  // open: clk, ValM, ValE, icode, rA, rB, ValA, ValB

  // Notes on the sheet:
  //   account for the frequency of the clock by the worst case scenario of instruction (idk how to calculate)
endmodule

module fetch (
  input  clk,
  input  [11:0] PC,
  output [3:0] icode,
  output [3:0] ifun,
  output [3:0] rA,
  output [3:0] rB,
  output [63:0] valC,
  output [11:0] ValP
);

  wire need_regids_1_true, need_valc_1_true;
  wire [7:0] instruction_memory_1_byte1, instruction_memory_1_byte2, instruction_memory_1_byte3,
       instruction_memory_1_byte4, instruction_memory_1_byte5, instruction_memory_1_byte6,
       instruction_memory_1_byte7, instruction_memory_1_byte8, instruction_memory_1_byte9;

  Instruction_Memory instruction_memory_1 (
    .PC(PC), .clk(clk), .Byte0({icode, ifun}), .Byte1(instruction_memory_1_byte1),
    .Byte2(instruction_memory_1_byte2), .Byte3(instruction_memory_1_byte3),
    .Byte4(instruction_memory_1_byte4), .Byte5(instruction_memory_1_byte5),
    .Byte6(instruction_memory_1_byte6), .Byte7(instruction_memory_1_byte7),
    .Byte8(instruction_memory_1_byte8), .Byte9(instruction_memory_1_byte9));
  Need_valC need_valc_1 (.icode(icode), .true(need_valc_1_true));
  Need_regIDs need_regids_1 (.icode(icode), .true(need_regids_1_true));
  Align align_1 (
    .icode(icode), .Byte1(instruction_memory_1_byte1), .Byte2(instruction_memory_1_byte2),
    .Byte3(instruction_memory_1_byte3), .Byte4(instruction_memory_1_byte4),
    .Byte5(instruction_memory_1_byte5), .Byte6(instruction_memory_1_byte6),
    .Byte7(instruction_memory_1_byte7), .Byte8(instruction_memory_1_byte8),
    .Byte9(instruction_memory_1_byte9), .rA(rA), .rB(rB), .valC(valC));
  PC_Increment pc_increment_1 (.Need_ValC(need_valc_1_true), .Need_RegIDs(need_regids_1_true), .PC(PC), .ValP(ValP));

  // Notes on the sheet:
  //   ValP = PC + 1 + Need_regIDs + Need_ValC * 8
endmodule

module Instruction_Memory (
  input  [11:0] PC,
  input  clk,
  output [7:0] Byte0,
  output [7:0] Byte1,
  output [7:0] Byte2,
  output [7:0] Byte3,
  output [7:0] Byte4,
  output [7:0] Byte5,
  output [7:0] Byte6,
  output [7:0] Byte7,
  output [7:0] Byte8,
  output [7:0] Byte9
);

  wire decoder_1_out1, decoder_1_out2, decoder_1_out3, decoder_1_out4, decoder_1_out5, decoder_1_out6,
       decoder_1_out7, decoder_1_out8, decoder_1_out9, decoder_1_out10;
  wire [3:0] counter_2_q;
  wire [7:0] demultiplexer_1_out1, demultiplexer_1_out2, demultiplexer_1_out3, demultiplexer_1_out4,
       demultiplexer_1_out5, demultiplexer_1_out6, demultiplexer_1_out7, demultiplexer_1_out8,
       demultiplexer_1_out9, demultiplexer_1_out10, ram_1_dout;
  wire [11:0] adder_1_out, counter_1_q;

  Counter #(.max('h9), .width(12)) counter_1 (.clk(clk), .Q(counter_1_q));  // open: clr, load, up, count, D, carry
  Adder #(.width(12)) adder_1 (.a(PC), .b(counter_1_q), .out(adder_1_out));  // open: cin, cout
  RAM #(.addrWidth(12)) ram_1 (.addr(adder_1_out), .clk(clk), .dout(ram_1_dout));  // open: we, oe, din
  Counter #(.max('h9), .width(4)) counter_2 (.clk(clk), .Q(counter_2_q));  // open: clr, load, up, count, D, carry
  Demultiplexer #(.select(4), .width(8)) demultiplexer_1 (
    .out1(demultiplexer_1_out1), .out2(demultiplexer_1_out2), .out3(demultiplexer_1_out3),
    .out4(demultiplexer_1_out4), .out5(demultiplexer_1_out5), .out6(demultiplexer_1_out6),
    .out7(demultiplexer_1_out7), .out8(demultiplexer_1_out8), .out9(demultiplexer_1_out9),
    .out10(demultiplexer_1_out10), .in(ram_1_dout), .sel(counter_2_q));  // open: out0, out11, out12, out13, out14, out15
  Decoder #(.select(4)) decoder_1 (
    .out1(decoder_1_out1), .out2(decoder_1_out2), .out3(decoder_1_out3), .out4(decoder_1_out4),
    .out5(decoder_1_out5), .out6(decoder_1_out6), .out7(decoder_1_out7), .out8(decoder_1_out8),
    .out9(decoder_1_out9), .out10(decoder_1_out10), .sel(counter_2_q));  // open: out0, out11, out12, out13, out14, out15, en
  Register register_1 (.D(demultiplexer_1_out1), .en(decoder_1_out1), .clk(clk), .Q(Byte0));  // open: clr
  Register register_2 (.D(demultiplexer_1_out2), .en(decoder_1_out2), .clk(clk), .Q(Byte1));  // open: clr
  Register register_3 (.D(demultiplexer_1_out3), .en(decoder_1_out3), .clk(clk), .Q(Byte2));  // open: clr
  Register register_4 (.D(demultiplexer_1_out4), .en(decoder_1_out4), .clk(clk), .Q(Byte3));  // open: clr
  Register register_5 (.D(demultiplexer_1_out5), .en(decoder_1_out5), .clk(clk), .Q(Byte4));  // open: clr
  Register register_6 (.D(demultiplexer_1_out6), .en(decoder_1_out6), .clk(clk), .Q(Byte5));  // open: clr
  Register register_7 (.D(demultiplexer_1_out7), .en(decoder_1_out7), .clk(clk), .Q(Byte6));  // open: clr
  Register register_8 (.D(demultiplexer_1_out8), .en(decoder_1_out8), .clk(clk), .Q(Byte7));  // open: clr
  Register register_9 (.D(demultiplexer_1_out9), .en(decoder_1_out9), .clk(clk), .Q(Byte8));  // open: clr
  Register register_10 (.D(demultiplexer_1_out10), .en(decoder_1_out10), .clk(clk), .Q(Byte9));  // open: clr
endmodule

module Align (
  input  [3:0] icode,
  input  [7:0] Byte1,
  input  [7:0] Byte2,
  input  [7:0] Byte3,
  input  [7:0] Byte4,
  input  [7:0] Byte5,
  input  [7:0] Byte6,
  input  [7:0] Byte7,
  input  [7:0] Byte8,
  input  [7:0] Byte9,
  output [3:0] rA,
  output [3:0] rB,
  output [63:0] valC
);

  wire decoder_1_out3, decoder_1_out7, decoder_1_out8, decoder_1_out10, decoder_1_out11, or_1_out, or_2_out,
       or_3_out;

  Decoder #(.select(4)) decoder_1 (
    .out3(decoder_1_out3), .out7(decoder_1_out7), .out8(decoder_1_out8), .out10(decoder_1_out10),
    .out11(decoder_1_out11), .sel(icode));  // open: out0, out1, out2, out4, out5, out6, out9, out12, out13, out14, out15, en
  Multiplexer #(.width(4)) multiplexer_1 (.in0(Byte1[7:4]), .in1(4'b1111), .out(rA), .sel(or_1_out));
  or or_1 (or_1_out, decoder_1_out3, decoder_1_out7, decoder_1_out8);
  Multiplexer #(.width(4)) multiplexer_2 (.in0(Byte1[3:0]), .in1(4'b1111), .out(rB), .sel(or_2_out));
  or or_2 (or_2_out, decoder_1_out7, decoder_1_out8, decoder_1_out10, decoder_1_out11);
  Multiplexer #(.width(64)) multiplexer_3 (
    .in0({Byte9, Byte8, Byte7, Byte6, Byte5, Byte4, Byte3, Byte2}),
    .in1({Byte8, Byte7, Byte6, Byte5, Byte4, Byte3, Byte2, Byte1}), .out(valC), .sel(or_3_out));
  or or_3 (or_3_out, decoder_1_out7, decoder_1_out8);
endmodule

module Need_valC (
  input  [3:0] icode,
  output true
);

  wire decoder_1_out3, decoder_1_out4, decoder_1_out5, decoder_1_out7, decoder_1_out8;

  Decoder #(.select(4)) decoder_1 (
    .out3(decoder_1_out3), .out4(decoder_1_out4), .out5(decoder_1_out5), .out7(decoder_1_out7),
    .out8(decoder_1_out8), .sel(icode));  // open: out0, out1, out2, out6, out9, out10, out11, out12, out13, out14, out15, en
  or or_1 (true, decoder_1_out3, decoder_1_out4, decoder_1_out5, decoder_1_out7, decoder_1_out8);
endmodule

module Need_regIDs (
  input  [3:0] icode,
  output true
);

  wire decoder_1_out2, decoder_1_out3, decoder_1_out4, decoder_1_out5, decoder_1_out6, decoder_1_out10,
       decoder_1_out11;

  Decoder #(.select(4)) decoder_1 (
    .out2(decoder_1_out2), .out3(decoder_1_out3), .out4(decoder_1_out4), .out5(decoder_1_out5),
    .out6(decoder_1_out6), .out10(decoder_1_out10), .out11(decoder_1_out11), .sel(icode));  // open: out0, out1, out7, out8, out9, out12, out13, out14, out15, en
  or or_1 (true, decoder_1_out2, decoder_1_out3, decoder_1_out4, decoder_1_out5, decoder_1_out6, decoder_1_out10, decoder_1_out11);
endmodule

module PC_Increment (
  input  Need_ValC,
  input  Need_RegIDs,
  input  [11:0] PC,
  output [11:0] ValP
);

  wire [11:0] adder_1_out, adder_2_out, multiplexer_1_out, multiplexer_2_out;

  Multiplexer #(.width(12)) multiplexer_1 (.in0({12{1'b0}}), .in1(12'h1), .out(multiplexer_1_out), .sel(Need_RegIDs));
  Adder #(.width(12)) adder_1 (.a(12'h1), .b(PC), .out(adder_1_out));  // open: cin, cout
  Multiplexer #(.width(12)) multiplexer_2 (.in0({12{1'b0}}), .in1(12'h8), .out(multiplexer_2_out), .sel(Need_ValC));
  Adder #(.width(12)) adder_2 (.a(multiplexer_1_out), .b(adder_1_out), .out(adder_2_out));  // open: cin, cout
  Adder #(.width(12)) adder_3 (.a(multiplexer_2_out), .b(adder_2_out), .out(ValP));  // open: cin, cout
endmodule

module decode (
  input  clk,
  input  [3:0] ValM,
  input  [3:0] ValE,
  input  [3:0] icode,
  input  [3:0] rA,
  input  [3:0] rB,
  output [3:0] ValA,
  output [3:0] ValB
);

  DstE dste_1 (.rB(rB), .icode(icode));  // open: E
  DstM dstm_1 (.rA(rA), .icode(icode));  // open: M
  SrcA srca_1 (.rA(rA), .icode(icode));  // open: A
  // Register_file register_file_1: pin names not known; wires that end beside it: clk, ValA, ValB
  SrcB srcb_1 (.rB(rB), .icode(icode));  // open: B
endmodule

module Register_file (
  input  clk,
  input  [3:0] srcA,
  input  [3:0] srcB,
  input  r_enable,
  input  enable,
  input  [3:0] dstE,
  input  [3:0] dstM,
  output [31:0] E,
  output [31:0] M,
  output [31:0] A,
  output [31:0] B
);

  wire decoder_1_out0, decoder_1_out1, decoder_1_out2, decoder_1_out3, decoder_1_out4, decoder_1_out5,
       decoder_1_out6, decoder_1_out7, decoder_2_out0, decoder_2_out1, decoder_2_out2, decoder_2_out3,
       decoder_2_out4, decoder_2_out5, decoder_2_out6, decoder_3_out0, decoder_3_out1, decoder_3_out2,
       decoder_3_out3, decoder_3_out4, decoder_3_out5, decoder_3_out6, decoder_3_out7, decoder_4_out0,
       decoder_4_out1, decoder_4_out2, decoder_4_out3, decoder_4_out4, decoder_4_out5, decoder_4_out6,
       undriven, undriven_2, undriven_3, undriven_4, undriven_5, undriven_6, undriven_7, undriven_8;
  wire [31:0] controlled_buffer_1_out, controlled_buffer_2_out, controlled_buffer_3_out,
       controlled_buffer_4_out, controlled_buffer_5_out, controlled_buffer_6_out, controlled_buffer_7_out,
       controlled_buffer_8_out, controlled_buffer_9_out, controlled_buffer_10_out, controlled_buffer_11_out,
       controlled_buffer_12_out, controlled_buffer_13_out, controlled_buffer_14_out,
       controlled_buffer_15_out, eax_q, ebp_q, ebx_q, ecx_q, edi_q, edx_q, esi_q, esp_q, r8_q, r9_q, r10_q,
       r11_q, r12_q, r13_q, r14_q, undriven_9;

  Decoder #(.select(4)) decoder_1 (
    .out0(decoder_1_out0), .out1(decoder_1_out1), .out2(decoder_1_out2), .out3(decoder_1_out3),
    .out4(decoder_1_out4), .out5(decoder_1_out5), .out6(decoder_1_out6), .out7(decoder_1_out7), .sel(dstE),
    .en(enable));  // open: out8, out9, out10, out11, out12, out13, out14, out15
  Decoder #(.select(4)) decoder_2 (
    .out0(decoder_2_out0), .out1(decoder_2_out1), .out2(decoder_2_out2), .out3(decoder_2_out3),
    .out4(decoder_2_out4), .out5(decoder_2_out5), .out6(decoder_2_out6), .sel(dstM), .en(enable));  // open: out7, out8, out9, out10, out11, out12, out13, out14, out15
  assign controlled_buffer_1_out = decoder_1_out0 ? E : 32'bz;  // Controlled_Buffer controlled_buffer_1
  assign controlled_buffer_2_out = decoder_1_out1 ? E : 32'bz;  // Controlled_Buffer controlled_buffer_2
  assign controlled_buffer_3_out = decoder_1_out2 ? E : 32'bz;  // Controlled_Buffer controlled_buffer_3
  assign controlled_buffer_4_out = decoder_1_out3 ? E : 32'bz;  // Controlled_Buffer controlled_buffer_4
  assign controlled_buffer_5_out = decoder_1_out4 ? E : 32'bz;  // Controlled_Buffer controlled_buffer_5
  assign controlled_buffer_6_out = decoder_1_out5 ? E : 32'bz;  // Controlled_Buffer controlled_buffer_6
  assign controlled_buffer_7_out = decoder_1_out6 ? E : 32'bz;  // Controlled_Buffer controlled_buffer_7
  assign controlled_buffer_8_out = decoder_1_out7 ? E : 32'bz;  // Controlled_Buffer controlled_buffer_8
  assign controlled_buffer_9_out = decoder_2_out0 ? M : 32'bz;  // Controlled_Buffer controlled_buffer_9
  assign controlled_buffer_10_out = decoder_2_out1 ? M : 32'bz;  // Controlled_Buffer controlled_buffer_10
  assign controlled_buffer_11_out = decoder_2_out2 ? M : 32'bz;  // Controlled_Buffer controlled_buffer_11
  assign controlled_buffer_12_out = decoder_2_out3 ? M : 32'bz;  // Controlled_Buffer controlled_buffer_12
  assign controlled_buffer_13_out = decoder_2_out4 ? M : 32'bz;  // Controlled_Buffer controlled_buffer_13
  assign controlled_buffer_14_out = decoder_2_out5 ? M : 32'bz;  // Controlled_Buffer controlled_buffer_14
  assign controlled_buffer_15_out = decoder_2_out6 ? M : 32'bz;  // Controlled_Buffer controlled_buffer_15
  Register #(.width(32)) eax (.D(controlled_buffer_1_out), .clk(clk), .Q(eax_q));  // open: en, clr
  Register #(.width(32)) ecx (.D(controlled_buffer_2_out), .clk(clk), .Q(ecx_q));  // open: en, clr
  Register #(.width(32)) edx (.D(controlled_buffer_3_out), .clk(clk), .Q(edx_q));  // open: en, clr
  Register #(.width(32)) ebx (.D(controlled_buffer_4_out), .clk(clk), .Q(ebx_q));  // open: en, clr
  Register #(.width(32)) esp (.D(controlled_buffer_5_out), .clk(clk), .Q(esp_q));  // open: en, clr
  Register #(.width(32)) ebp (.D(controlled_buffer_6_out), .clk(clk), .Q(ebp_q));  // open: en, clr
  Register #(.width(32)) esi (.D(controlled_buffer_7_out), .clk(clk), .Q(esi_q));  // open: en, clr
  Register #(.width(32)) edi (.D(controlled_buffer_8_out), .clk(clk), .Q(edi_q));  // open: en, clr
  Register #(.width(32)) r8 (.D(controlled_buffer_9_out), .clk(clk), .Q(r8_q));  // open: en, clr
  Register #(.width(32)) r9 (.D(controlled_buffer_10_out), .clk(clk), .Q(r9_q));  // open: en, clr
  Register #(.width(32)) r10 (.D(controlled_buffer_11_out), .clk(clk), .Q(r10_q));  // open: en, clr
  Register #(.width(32)) r11 (.D(controlled_buffer_12_out), .clk(clk), .Q(r11_q));  // open: en, clr
  Register #(.width(32)) r12 (.D(controlled_buffer_13_out), .clk(clk), .Q(r12_q));  // open: en, clr
  Register #(.width(32)) r13 (.D(controlled_buffer_14_out), .clk(clk), .Q(r13_q));  // open: en, clr
  Register #(.width(32)) r14 (.D(controlled_buffer_15_out), .clk(clk), .Q(r14_q));  // open: en, clr
  assign A = decoder_3_out0 ? eax_q : 32'bz;  // Controlled_Buffer controlled_buffer_16
  assign A = decoder_3_out1 ? ecx_q : 32'bz;  // Controlled_Buffer controlled_buffer_17
  assign A = decoder_3_out2 ? edx_q : 32'bz;  // Controlled_Buffer controlled_buffer_18
  assign A = decoder_3_out3 ? ebx_q : 32'bz;  // Controlled_Buffer controlled_buffer_19
  assign A = decoder_3_out4 ? esp_q : 32'bz;  // Controlled_Buffer controlled_buffer_20
  assign A = decoder_3_out5 ? ebp_q : 32'bz;  // Controlled_Buffer controlled_buffer_21
  assign A = decoder_3_out6 ? esi_q : 32'bz;  // Controlled_Buffer controlled_buffer_22
  assign A = decoder_3_out7 ? edi_q : 32'bz;  // Controlled_Buffer controlled_buffer_23
  assign B = decoder_4_out0 ? r8_q : 32'bz;  // Controlled_Buffer controlled_buffer_24
  assign B = decoder_4_out1 ? r9_q : 32'bz;  // Controlled_Buffer controlled_buffer_25
  assign B = decoder_4_out2 ? r10_q : 32'bz;  // Controlled_Buffer controlled_buffer_26
  assign B = decoder_4_out3 ? r11_q : 32'bz;  // Controlled_Buffer controlled_buffer_27
  assign B = decoder_4_out4 ? r12_q : 32'bz;  // Controlled_Buffer controlled_buffer_28
  assign B = decoder_4_out5 ? r13_q : 32'bz;  // Controlled_Buffer controlled_buffer_29
  assign B = decoder_4_out6 ? r14_q : 32'bz;  // Controlled_Buffer controlled_buffer_30
  Decoder #(.select(4)) decoder_3 (
    .out0(decoder_3_out0), .out1(decoder_3_out1), .out2(decoder_3_out2), .out3(decoder_3_out3),
    .out4(decoder_3_out4), .out5(decoder_3_out5), .out6(decoder_3_out6), .out7(decoder_3_out7), .sel(srcA),
    .en(r_enable));  // open: out8, out9, out10, out11, out12, out13, out14, out15
  Decoder #(.select(4)) decoder_4 (
    .out0(decoder_4_out0), .out1(decoder_4_out1), .out2(decoder_4_out2), .out3(decoder_4_out3),
    .out4(decoder_4_out4), .out5(decoder_4_out5), .out6(decoder_4_out6), .sel(srcB), .en(r_enable));  // open: out7, out8, out9, out10, out11, out12, out13, out14, out15
  Controlled_Buffer #(.width(32)) controlled_buffer_31 (.in(undriven_9), .en(undriven));  // open: out
  Controlled_Buffer #(.width(32)) controlled_buffer_32 (.in(undriven_9), .en(undriven_2));  // open: out
  Controlled_Buffer #(.width(32)) controlled_buffer_33 (.in(undriven_9), .en(undriven_3));  // open: out
  Controlled_Buffer #(.width(32)) controlled_buffer_34 (.in(undriven_9), .en(undriven_4));  // open: out
  Controlled_Buffer #(.width(32)) controlled_buffer_35 (.in(undriven_9), .en(undriven_5));  // open: out
  Controlled_Buffer #(.width(32)) controlled_buffer_36 (.in(undriven_9), .en(undriven_6));  // open: out
  Controlled_Buffer #(.width(32)) controlled_buffer_37 (.in(undriven_9), .en(undriven_7));  // open: out
  Controlled_Buffer #(.width(32)) controlled_buffer_38 (.in(undriven_9), .en(undriven_8));  // open: out
endmodule

module DstE (
  input  [3:0] rB,
  input  [3:0] icode,
  output [3:0] E
);

  Multiplexer #(.select(4), .width(4)) multiplexer_1 (
    .in0(4'b1111), .in1(4'b1111), .in2(rB), .in3(rB), .in4(4'b1111), .in5(4'b1111), .in6(rB), .in7(4'b1111),
    .in8(4'b0100), .in9(4'b0100), .in10(4'b0100), .in11(4'b0100), .out(E), .sel(icode));  // open: in12, in13, in14, in15
endmodule

module DstM (
  input  [3:0] rA,
  input  [3:0] icode,
  output [3:0] M
);

  Multiplexer #(.select(4), .width(4)) multiplexer_1 (
    .in0(4'b1111), .in1(4'b1111), .in2(4'b1111), .in3(4'b1111), .in4(4'b1111), .in5(rA), .in6(4'b1111),
    .in7(4'b1111), .in8(4'b1111), .in9(4'b1111), .in10(4'b1111), .in11(rA), .out(M), .sel(icode));  // open: in12, in13, in14, in15
endmodule

module SrcA (
  input  [3:0] rA,
  input  [3:0] icode,
  output [3:0] A
);

  Multiplexer #(.select(4), .width(4)) multiplexer_1 (
    .in0(4'b1111), .in1(4'b1111), .in2(rA), .in3(4'b1111), .in4(rA), .in5(4'b1111), .in6(rA), .in7(4'b1111),
    .in8(4'b0100), .in9(4'b0100), .in10(rA), .in11(4'b0100), .out(A), .sel(icode));  // open: in12, in13, in14, in15
endmodule

module SrcB (
  input  [3:0] rB,
  input  [3:0] icode,
  output [3:0] B
);

  Multiplexer #(.select(4), .width(4)) multiplexer_1 (
    .in0(4'b1111), .in1(4'b1111), .in2(4'b1111), .in3(4'b1111), .in4(rB), .in5(rB), .in6(4'b1111),
    .in7(4'b1111), .in8(4'b0100), .in9(4'b0100), .in10(4'b0100), .in11(4'b0100), .out(B), .sel(icode));  // open: in12, in13, in14, in15
endmodule
